# Fritzing sketch v2_layout (saved by Fritzing 1.0.6)
breadboards: 1

parts:
  ESP32-S3_Mini_(MCU) = ESP32-S3 zero
  LSM6DS3_(IMU) = LSM303C (6 DOF)
  D1 = Schottky Diode [part_number=1N5817 package="300 mil [THT]"]
  WWZMDiB_(SD_Card) = MicroSD Card Module
  4_7_LIPO_500_MAH_(BATTERY) = LIPO-1000mAh [package=lipo-1000]
  R1_100k = Resistor [tolerance=±5% power=0.25W resistance=220 package=THT]
  R2_100k = Resistor [tolerance=±5% power=0.25W resistance=220 package=THT]
  TP4057_(POWER) = TP4056 [chip_label=TP4056 package="DIP (Dual Inline) [THT]"]

nets:
  N1: ESP32-S3_Mini_(MCU).Pin_1, D1.cathode
  GND: ESP32-S3_Mini_(MCU).Pin_2, LSM6DS3_(IMU).GND, WWZMDiB_(SD_Card).GND, R2_100k.Pin_0, TP4057_(POWER).OUT-
  VCC: ESP32-S3_Mini_(MCU).Pin_3, LSM6DS3_(IMU).VCC, WWZMDiB_(SD_Card).VCC
  N2: ESP32-S3_Mini_(MCU).Pin_4, LSM6DS3_(IMU).SCL/SCLK
  N3: ESP32-S3_Mini_(MCU).Pin_5, LSM6DS3_(IMU).SDA/SDI/SDO
  N4: ESP32-S3_Mini_(MCU).Pin_7, R1_100k.Pin_0, R2_100k.Pin_1
  N5: ESP32-S3_Mini_(MCU).Pin_24, WWZMDiB_(SD_Card).SCK
  N6: ESP32-S3_Mini_(MCU).Pin_25, WWZMDiB_(SD_Card).MOSI
  N7: ESP32-S3_Mini_(MCU).Pin_26, WWZMDiB_(SD_Card).MISO
  N8: ESP32-S3_Mini_(MCU).Pin_27, WWZMDiB_(SD_Card).CS
  N9: D1.anode, TP4057_(POWER).OUT+
  N10: 4_7_LIPO_500_MAH_(BATTERY).+, R1_100k.Pin_1, TP4057_(POWER).BAT+
  N11: 4_7_LIPO_500_MAH_(BATTERY).-, TP4057_(POWER).BAT-

custom parts:
  ESP32-S3 zero: ESP32-S3 Mini Development Board, Based on ESP32-S3FH4R2 Dual-Core Processor, 240MHz Running Frequency, 2.4GHz Wi-Fi & Bluetooth 5.
  TP4056: A DIP stand-in part for whatever IC you want. With 6 pins on a 300mil dual inline package (DIP) footprint.
